// Digital circuit ex3.dig as structural Verilog
module ex3 (
  input  [1:0] A,
  input  [1:0] B,
  output Y
);

  wire EQ, GT0, notB0, notB1, T1, T2, X1;

  not not_1 (notB0, B[0]);
  not not_2 (notB1, B[1]);
  and and_1 (T1, A[1], notB1);
  xor xor_1 (X1, A[1], B[1]);
  and and_2 (GT0, A[0], notB0);
  not not_3 (EQ, X1);
  and and_3 (T2, EQ, GT0);
  or or_1 (Y, T1, T2);
endmodule

/* Test case EX3 Test:
A B Y 

 0b00 0b00 0
 0b00 0b01 0
 0b00 0b10 0
 0b00 0b11 0
 0b01 0b00 1
 0b01 0b01 0
 0b01 0b10 0
 0b01 0b11 0
 0b10 0b00 1
 0b10 0b01 1
 0b10 0b10 0
 0b10 0b11 0
 0b11 0b00 1
 0b11 0b01 1
 0b11 0b10 1
 0b11 0b11 0
*/
