// Digital circuit Lab02 - 副本.dig as structural Verilog
module \Lab02___副本  (
  input  B,
  input  C,
  input  A,
  input  D,
  output Fa,
  output Fb,
  output Fc,
  output Fd,
  output Fe,
  output Fg,
  output Ff
);

  wire A_t, and_1_out, and_2_out, and_3_out, and_4_out, and_5_out, and_6_out, and_7_out, and_8_out,
       and_9_out, and_10_out, and_11_out, and_12_out, and_13_out, and_14_out, and_15_out, and_16_out,
       and_17_out, and_18_out, B_t, C_t, D_t;

  not not_1 (A_t, A);
  not not_2 (B_t, B);
  not not_3 (C_t, C);
  not not_4 (D_t, D);
  Seven_Seg seven_seg_1 (.a(Fa), .b(Fb), .c(Fc), .d(Fd), .e(Fe), .f(Ff), .g(Fg), .dp(1'b0));
  and and_1 (and_1_out, A_t, B_t, D_t);
  and and_2 (and_2_out, A, B_t, C_t);
  and and_3 (and_3_out, A_t, B, D);
  and and_4 (and_4_out, C_t, D_t);
  and and_5 (and_5_out, C, D);
  and and_6 (and_6_out, B_t, C);
  and and_7 (and_7_out, C_t, D_t);
  and and_8 (and_8_out, B, C_t, D);
  and and_9 (and_9_out, A_t, C_t);
  or or_1 (Fa, C, and_1_out, and_2_out, and_3_out);
  or or_2 (Fb, B_t, and_4_out, and_5_out);
  or or_3 (Fc, B, D, A_t);
  or or_4 (Fd, and_6_out, and_7_out, and_8_out, and_9_out);
  and and_10 (and_10_out, C_t, D_t);
  and and_11 (and_11_out, A_t, B_t, D_t);
  and and_12 (and_12_out, A_t, C_t, D_t);
  and and_13 (and_13_out, B_t, C_t, D_t);
  and and_14 (and_14_out, A_t, B, C);
  and and_15 (and_15_out, A, B_t, C_t);
  and and_16 (and_16_out, A_t, B);
  and and_17 (and_17_out, A, B_t, C_t);
  and and_18 (and_18_out, B_t, C_t, D_t);
  or or_5 (Fe, and_10_out, and_11_out);
  or or_6 (Ff, and_12_out, and_13_out, and_14_out, and_15_out);
  or or_7 (Fg, C, and_16_out, and_17_out, and_18_out);
endmodule

/* Test case test:
A	B	C	D		Fa	Fb	Fc	Fd	Fe	Ff	Fg
0	0	0	0		1	1	1	1	1	1	0
0	0	0	1		0	1	1	0	0	0	0
0	0	1	0		1	1	0	1	1	0	1
0	0	1	1		1	1	1	1	0	0	1
0	1	0	0		0	1	1	0	0	1	1
0	1	0	1		1	0	1	1	0	1	1
0	1	1	0		1	0	1	1	1	1	1
0	1	1	1		1	1	1	0	0	0	0
1	0	0	0		1	1	1	1	1	1	1
1	0	0	1		1	1	1	1	0	1	1
1	0	1	0		1	1	1	0	1	1	1
1	0	1	1		0	0	1	1	1	1	1
1	1	0	0		0	0	0	1	1	0	1
1	1	0	1		0	1	1	1	1	0	1
1	1	1	0		1	0	0	1	1	1	1
1	1	1	1		1	0	0	0	1	1	1
*/
