// Digital circuit control-unit.dig as structural Verilog
module control_unit (
  input  [6:0] opcode,
  input  [2:0] funct3,
  input  [6:0] funct7,
  output RegWrite,
  output ALUSrc,
  output [1:0] ImmSrc,
  output [3:0] ALUOp
);

  wire f3_000, f3_010, f3_110, f3_111, f7_0000000, f7_0100000, is_add, is_addi, is_and, is_andi, is_or,
       is_slt, is_slti, is_sub, isI, isR;
  wire [2:0] A;

  Comparator #(.Bits(7)) comparator_1 (.a(opcode), .b(7'b0110011), .eq(isR));  // open: gt, lt
  Comparator #(.Bits(7)) comparator_2 (.a(opcode), .b(7'b0010011), .eq(isI));  // open: gt, lt
  Comparator #(.Bits(3)) funct3_add_sub_addi (.a(funct3), .b(3'b000), .eq(f3_000));  // open: gt, lt
  Comparator #(.Bits(3)) funct3_and_andi (.a(funct3), .b(3'b111), .eq(f3_111));  // open: gt, lt
  Comparator #(.Bits(3)) funct3_or (.a(funct3), .b(3'b110), .eq(f3_110));  // open: gt, lt
  Comparator #(.Bits(3)) funct3_slt_slti (.a(funct3), .b(3'b010), .eq(f3_010));  // open: gt, lt
  Comparator #(.Bits(7)) normal_R_type (.a(funct7), .b({7{1'b0}}), .eq(f7_0000000));  // open: gt, lt
  Comparator #(.Bits(7)) sub (.a(funct7), .b(7'b0100000), .eq(f7_0100000));  // open: gt, lt
  and and_1 (is_add, isR, f3_000, f7_0000000);
  and and_2 (is_sub, isR, f3_000, f7_0100000);
  and and_3 (is_and, isR, f3_111, f7_0000000);
  and and_4 (is_or, isR, f3_110, f7_0000000);
  and and_5 (is_slt, isR, f3_010, f7_0000000);
  and and_6 (is_addi, isI, f3_000);
  and and_7 (is_slti, isI, f3_010);
  and and_8 (is_andi, isI, f3_111);
  PriorityEncoder #(.Selector_Bits(3)) priorityencoder_1 (
    .in0(is_add), .in1(is_sub), .in2(is_and), .in3(is_or), .in4(is_slt), .in5(is_addi), .in6(is_slti),
    .in7(is_andi), .num(A));  // open: any
  ROM #(.AddrBits(3), .Bits(8)) rom_1 (.A(A), .sel(1'b1), .D({RegWrite, ALUSrc, ImmSrc, ALUOp}));

  // Other names for the same wires on the sheet: ROM[7:0] = {RegWrite, ALUSrc, ImmSrc, ALUOp}

  // Notes on the sheet:
  //   contents of rom_1 (hex, n*v repeats v):
  //   82,86,80,81,87,c2,c7,c0
endmodule
