// Digital circuit cpu.dig as structural Verilog
module cpu (
  input  clk,
  output [31:0] ReadData1,
  output [31:0] ReadData2
);

  wire ALUSrc, RegWrite;
  wire [1:0] ImmSrc;
  wire [3:0] ALUOp;
  wire [31:0] add_1_s, ALUB, D, PC_q, WriteData;

  control_unit control_unit_1 (
    .opcode(D[6:0]), .funct3(D[14:12]), .funct7(D[31:25]), .RegWrite(RegWrite), .ALUSrc(ALUSrc),
    .ImmSrc(ImmSrc), .ALUOp(ALUOp));
  alu alu_1 (.A(ReadData1), .B(ALUB), .ALUOp(ALUOp), .Result(WriteData));  // open: FlagZ
  Multiplexer #(.Bits(32)) multiplexer_1 (.sel(ALUSrc), .in_0(ReadData2), .in_1({{21{D[31]}}, D[30:20]}), .out(ALUB));
  Register #(.Bits(32), .isProgramCounter("true")) PC (.D(add_1_s), .C(clk), .en(1'b1), .Q(PC_q));
  Add #(.Bits(32)) add_1 (.a(32'h4), .b(PC_q), .c_i(1'b0), .s(add_1_s));  // open: c_o
  ROM #(.AddrBits(10), .isProgramMemory("true"), .Bits(32)) Instruction_Memory (.A(PC_q[11:2]), .sel(1'b1), .D(D));
  register_file register_file_1 (
    .ReadReg1(D[19:15]), .ReadReg2(D[24:20]), .WriteReg(D[11:7]), .WriteData(WriteData), .RegWrite(RegWrite),
    .Clock(clk), .ReadData1(ReadData1), .ReadData2(ReadData2));

  // Other names for the same wires on the sheet: clock = clk; opcode[6:0] = D[6:0]; rd[4:0] = D[11:7];
  //   funct3[2:0] = D[14:12]; rs1[4:0] = D[19:15]; imm12[11:0] = D[31:20]; imm32[31:0] = {{21{D[31]}}, D[30:20]};
  //   rs2[4:0] = D[24:20]; funct7[6:0] = D[31:25]; sign = D[31]; rd1[31:0] = ReadData1; rd2[31:0] = ReadData2

  // Notes on the sheet:
  //   contents of Instruction_Memory (hex, n*v repeats v):
  //   fec00213,7f020293,70128313,53130393,12337713,71c77793,5417f893
  //   ,13722913,292993,9aa13,ffda2a93,5aab13,b0013,fec22b93,b8013,fa65ac13
  //   ,c0013,22c93,c8013,2585ad13,d0013,fff22d93,d8013
endmodule

/* Test case cpu:
clk ReadData1 ReadData2
0 0 0
C (-20) 0
C 2012 0
C 3805 0
C 3805 0
C 1 0
C 0 0
C (-20) 0
C 1 0
C 1 0
C 0 0
C 0 2012
C 1 0
C (-20) 0
C 0 0
C 0 3805
C 0 0
C (-20) 0
C 1 0
C 0 0
C 1 0
C (-20) 0
C 1 0
*/
