// Digital circuit slt-unit.dig as structural Verilog
module slt_unit (
  input  Sign,
  input  Overflow,
  output Result
);

  xor xor_1 (Result, Sign, Overflow);
endmodule

/* Test case SLT Test:
Sign Overflow Result
0 0 0
0 1 1
1 0 1
1 1 0
*/
