// Digital circuit register-file.dig as structural Verilog
module register_file (
  input  [4:0] ReadReg1,
  input  [4:0] ReadReg2,
  input  [4:0] WriteReg,
  input  [31:0] WriteData,
  input  RegWrite,
  input  Clock,
  output [31:0] ReadData1,
  output [31:0] ReadData2
);

  wire and_1_out, and_2_out, and_3_out, and_4_out, and_5_out, and_6_out, and_7_out, and_8_out, and_9_out,
       and_10_out, and_11_out, and_12_out, and_13_out, and_14_out, and_15_out, and_16_out, and_17_out,
       and_18_out, and_19_out, and_20_out, and_21_out, and_22_out, and_23_out, and_24_out, and_25_out,
       and_26_out, and_27_out, and_28_out, and_29_out, and_30_out, and_31_out, op0, op1, op2, op3, op4, op5,
       op6, op7, op8, op9, op10, op11, op12, op13, op14, op15, op16, op17, op18, op19, op20, op21, op22,
       op23, op24, op25, op26, op27, op28, op29, op30, op31;
  wire [31:0] q0, q1, q2, q3, q4, q5, q6, q7, q8, q9, q10, q11, q12, q13, q14, q15, q16, q17, q18, q19, q20,
       q21, q22, q23, q24, q25, q26, q27, q28, q29, q30, q31;

  Decoder #(.Selector_Bits(5)) decoder_1 (
    .sel(WriteReg), .out_0(op0), .out_1(op1), .out_2(op2), .out_3(op3), .out_4(op4), .out_5(op5),
    .out_6(op6), .out_7(op7), .out_8(op8), .out_9(op9), .out_10(op10), .out_11(op11), .out_12(op12),
    .out_13(op13), .out_14(op14), .out_15(op15), .out_16(op16), .out_17(op17), .out_18(op18), .out_19(op19),
    .out_20(op20), .out_21(op21), .out_22(op22), .out_23(op23), .out_24(op24), .out_25(op25), .out_26(op26),
    .out_27(op27), .out_28(op28), .out_29(op29), .out_30(op30), .out_31(op31));
  and and_1 (and_1_out, op1, RegWrite);
  and and_2 (and_2_out, op2, RegWrite);
  and and_3 (and_3_out, op3, RegWrite);
  and and_4 (and_4_out, op4, RegWrite);
  and and_5 (and_5_out, op5, RegWrite);
  and and_6 (and_6_out, op6, RegWrite);
  and and_7 (and_7_out, op7, RegWrite);
  Register #(.Bits(32)) Reg0 (.D(WriteData), .C(Clock), .en(1'b0), .Q(q0));
  Register #(.Bits(32)) Reg1 (.D(WriteData), .C(Clock), .en(and_1_out), .Q(q1));
  Register #(.Bits(32)) Reg2 (.D(WriteData), .C(Clock), .en(and_2_out), .Q(q2));
  Register #(.Bits(32)) Reg3 (.D(WriteData), .C(Clock), .en(and_3_out), .Q(q3));
  Register #(.Bits(32)) Reg4 (.D(WriteData), .C(Clock), .en(and_4_out), .Q(q4));
  Register #(.Bits(32)) Reg5 (.D(WriteData), .C(Clock), .en(and_5_out), .Q(q5));
  Register #(.Bits(32)) Reg6 (.D(WriteData), .C(Clock), .en(and_6_out), .Q(q6));
  Register #(.Bits(32)) Reg7 (.D(WriteData), .C(Clock), .en(and_7_out), .Q(q7));
  and and_8 (and_8_out, op8, RegWrite);
  and and_9 (and_9_out, op9, RegWrite);
  and and_10 (and_10_out, op10, RegWrite);
  and and_11 (and_11_out, op11, RegWrite);
  and and_12 (and_12_out, op12, RegWrite);
  and and_13 (and_13_out, op13, RegWrite);
  and and_14 (and_14_out, op14, RegWrite);
  and and_15 (and_15_out, op15, RegWrite);
  Register #(.Bits(32)) Reg8 (.D(WriteData), .C(Clock), .en(and_8_out), .Q(q8));
  Register #(.Bits(32)) Reg9 (.D(WriteData), .C(Clock), .en(and_9_out), .Q(q9));
  Register #(.Bits(32)) Reg10 (.D(WriteData), .C(Clock), .en(and_10_out), .Q(q10));
  Register #(.Bits(32)) Reg11 (.D(WriteData), .C(Clock), .en(and_11_out), .Q(q11));
  Register #(.Bits(32)) Reg12 (.D(WriteData), .C(Clock), .en(and_12_out), .Q(q12));
  Register #(.Bits(32)) Reg13 (.D(WriteData), .C(Clock), .en(and_13_out), .Q(q13));
  Register #(.Bits(32)) Reg14 (.D(WriteData), .C(Clock), .en(and_14_out), .Q(q14));
  Register #(.Bits(32)) Reg15 (.D(WriteData), .C(Clock), .en(and_15_out), .Q(q15));
  and and_16 (and_16_out, op16, RegWrite);
  and and_17 (and_17_out, op17, RegWrite);
  and and_18 (and_18_out, op18, RegWrite);
  and and_19 (and_19_out, op19, RegWrite);
  and and_20 (and_20_out, op20, RegWrite);
  and and_21 (and_21_out, op21, RegWrite);
  and and_22 (and_22_out, op22, RegWrite);
  and and_23 (and_23_out, op23, RegWrite);
  Register #(.Bits(32)) Reg16 (.D(WriteData), .C(Clock), .en(and_16_out), .Q(q16));
  Register #(.Bits(32)) Reg17 (.D(WriteData), .C(Clock), .en(and_17_out), .Q(q17));
  Register #(.Bits(32)) Reg18 (.D(WriteData), .C(Clock), .en(and_18_out), .Q(q18));
  Register #(.Bits(32)) Reg19 (.D(WriteData), .C(Clock), .en(and_19_out), .Q(q19));
  Register #(.Bits(32)) Reg20 (.D(WriteData), .C(Clock), .en(and_20_out), .Q(q20));
  Register #(.Bits(32)) Reg21 (.D(WriteData), .C(Clock), .en(and_21_out), .Q(q21));
  Register #(.Bits(32)) Reg22 (.D(WriteData), .C(Clock), .en(and_22_out), .Q(q22));
  Register #(.Bits(32)) Reg23 (.D(WriteData), .C(Clock), .en(and_23_out), .Q(q23));
  and and_24 (and_24_out, op24, RegWrite);
  and and_25 (and_25_out, op25, RegWrite);
  and and_26 (and_26_out, op26, RegWrite);
  and and_27 (and_27_out, op27, RegWrite);
  and and_28 (and_28_out, op28, RegWrite);
  and and_29 (and_29_out, op29, RegWrite);
  and and_30 (and_30_out, op30, RegWrite);
  and and_31 (and_31_out, op31, RegWrite);
  Register #(.Bits(32)) Reg24 (.D(WriteData), .C(Clock), .en(and_24_out), .Q(q24));
  Register #(.Bits(32)) Reg25 (.D(WriteData), .C(Clock), .en(and_25_out), .Q(q25));
  Register #(.Bits(32)) Reg26 (.D(WriteData), .C(Clock), .en(and_26_out), .Q(q26));
  Register #(.Bits(32)) Reg27 (.D(WriteData), .C(Clock), .en(and_27_out), .Q(q27));
  Register #(.Bits(32)) Reg28 (.D(WriteData), .C(Clock), .en(and_28_out), .Q(q28));
  Register #(.Bits(32)) Reg29 (.D(WriteData), .C(Clock), .en(and_29_out), .Q(q29));
  Register #(.Bits(32)) Reg30 (.D(WriteData), .C(Clock), .en(and_30_out), .Q(q30));
  Register #(.Bits(32)) Reg31 (.D(WriteData), .C(Clock), .en(and_31_out), .Q(q31));
  Multiplexer #(.Selector_Bits(5), .Bits(32)) multiplexer_1 (
    .sel(ReadReg1), .in_0({32{1'b0}}), .in_1(q1), .in_2(q2), .in_3(q3), .in_4(q4), .in_5(q5), .in_6(q6),
    .in_7(q7), .in_8(q8), .in_9(q9), .in_10(q10), .in_11(q11), .in_12(q12), .in_13(q13), .in_14(q14),
    .in_15(q15), .in_16(q16), .in_17(q17), .in_18(q18), .in_19(q19), .in_20(q20), .in_21(q21), .in_22(q22),
    .in_23(q23), .in_24(q24), .in_25(q25), .in_26(q26), .in_27(q27), .in_28(q28), .in_29(q29), .in_30(q30),
    .in_31(q31), .out(ReadData1));
  Multiplexer #(.Selector_Bits(5), .Bits(32)) multiplexer_2 (
    .sel(ReadReg2), .in_0({32{1'b0}}), .in_1(q1), .in_2(q2), .in_3(q3), .in_4(q4), .in_5(q5), .in_6(q6),
    .in_7(q7), .in_8(q8), .in_9(q9), .in_10(q10), .in_11(q11), .in_12(q12), .in_13(q13), .in_14(q14),
    .in_15(q15), .in_16(q16), .in_17(q17), .in_18(q18), .in_19(q19), .in_20(q20), .in_21(q21), .in_22(q22),
    .in_23(q23), .in_24(q24), .in_25(q25), .in_26(q26), .in_27(q27), .in_28(q28), .in_29(q29), .in_30(q30),
    .in_31(q31), .out(ReadData2));

  // Other names for the same wires on the sheet: clk = Clock; rd1[31:0] = ReadData1; rd2[31:0] = ReadData2;
  //   rr1[4:0] = ReadReg1; rr2[4:0] = ReadReg2; rw = RegWrite; wd[31:0] = WriteData; wr[4:0] = WriteReg
endmodule

/* Test case Register File Test:
WriteReg WriteData RegWrite Clock ReadReg1 ReadReg2 ReadData1 ReadData2

# $1 = 25
1 25 1 C 1 0 25 0

# $2 = 30
2 30 1 C 0 2 0 30

# $(N+1) = (N+1)
loop(N, 30)
	(N+1) (N+1) 1 C (N+1) (N) (N+1) (N)
end loop

# $(N+1) = N-60
loop(N, 30)
	(N+1) (N-60) 1 C (N+1) (N+1) (N-60) (N-60)
end loop

# Try writing to $0. This should not write anything
0 25 1 C 0 0 0 0

# try writing when RegWrite = 0
# (the registers should still have their old values)
loop(N, 30)
	(N+1) (N+80) 0 C (N+1) (N+1) (N-60) (N-60)
end loop
*/
